// Logisim project Floating Point Adder.circ as structural Verilog: 33 circuits, main circuit main
module main (
  input  [31:0] A,
  input  [31:0] B,
  output Overflow,
  output [31:0] A___B
);

  Floating_Point_Adder floating_point_adder_1 (.A(A), .B(B), .Y(A___B), .Overflow(Overflow));
endmodule

module _1_bit_RS (
  input  [24:0] S,
  input  Enable,
  output [24:0] out_3
);

  wire [24:0] Shifted;
  wire [27:0] bit_extender_1_out, bit_extender_2_out;
  wire [27:25] n28_bit_mux_1_y;

  assign bit_extender_1_out = {{3{1'b0}}, S};  // Bit_Extender bit_extender_1
  assign bit_extender_2_out = {{3{1'b0}}, Shifted};  // Bit_Extender bit_extender_2
  Shifter #(.width(25), .shift("lr")) shifter_1 (.in(S), .\dist (5'b00001), .out(Shifted));
  _28_Bit_MUX u_28_bit_mux_1 (.B(bit_extender_2_out), .Y({n28_bit_mux_1_y, out_3}), .A(bit_extender_1_out), .S(Enable));
endmodule

module _28_Bit_MUX (
  input  [27:0] B,
  input  [27:0] A,
  input  S,
  output [27:0] Y
);

  _74157 u_74157_1 (
    ._1__S(S), ._2__A1(A[0]), ._3__B1(B[0]), ._4__Y1(Y[0]), ._5__A2(A[1]), ._6__B2(B[1]), ._7__Y2(Y[1]),
    ._15__G(1'b0), ._14__A4(A[3]), ._13__B4(B[3]), ._12__Y4(Y[3]), ._11__A3(A[2]), ._10__B3(B[2]),
    ._9__Y3(Y[2]));  // open: _8__GND, _16__Vcc
  _74157 u_74157_2 (
    ._1__S(S), ._2__A1(A[4]), ._3__B1(B[4]), ._4__Y1(Y[4]), ._5__A2(A[5]), ._6__B2(B[5]), ._7__Y2(Y[5]),
    ._15__G(1'b0), ._14__A4(A[7]), ._13__B4(B[7]), ._12__Y4(Y[7]), ._11__A3(A[6]), ._10__B3(B[6]),
    ._9__Y3(Y[6]));  // open: _8__GND, _16__Vcc
  _74157 u_74157_3 (
    ._1__S(S), ._2__A1(A[8]), ._3__B1(B[8]), ._4__Y1(Y[8]), ._5__A2(A[9]), ._6__B2(B[9]), ._7__Y2(Y[9]),
    ._15__G(1'b0), ._14__A4(A[11]), ._13__B4(B[11]), ._12__Y4(Y[11]), ._11__A3(A[10]), ._10__B3(B[10]),
    ._9__Y3(Y[10]));  // open: _8__GND, _16__Vcc
  _74157 u_74157_4 (
    ._1__S(S), ._2__A1(A[12]), ._3__B1(B[12]), ._4__Y1(Y[12]), ._5__A2(A[13]), ._6__B2(B[13]),
    ._7__Y2(Y[13]), ._15__G(1'b0), ._14__A4(A[15]), ._13__B4(B[15]), ._12__Y4(Y[15]), ._11__A3(A[14]),
    ._10__B3(B[14]), ._9__Y3(Y[14]));  // open: _8__GND, _16__Vcc
  _74157 u_74157_5 (
    ._1__S(S), ._2__A1(A[16]), ._3__B1(B[16]), ._4__Y1(Y[16]), ._5__A2(A[17]), ._6__B2(B[17]),
    ._7__Y2(Y[17]), ._15__G(1'b0), ._14__A4(A[19]), ._13__B4(B[19]), ._12__Y4(Y[19]), ._11__A3(A[18]),
    ._10__B3(B[18]), ._9__Y3(Y[18]));  // open: _8__GND, _16__Vcc
  _74157 u_74157_6 (
    ._1__S(S), ._2__A1(A[20]), ._3__B1(B[20]), ._4__Y1(Y[20]), ._5__A2(A[21]), ._6__B2(B[21]),
    ._7__Y2(Y[21]), ._15__G(1'b0), ._14__A4(A[23]), ._13__B4(B[23]), ._12__Y4(Y[23]), ._11__A3(A[22]),
    ._10__B3(B[22]), ._9__Y3(Y[22]));  // open: _8__GND, _16__Vcc
  _74157 u_74157_7 (
    ._1__S(S), ._2__A1(A[24]), ._3__B1(B[24]), ._4__Y1(Y[24]), ._5__A2(A[25]), ._6__B2(B[25]),
    ._7__Y2(Y[25]), ._15__G(1'b0), ._14__A4(A[27]), ._13__B4(B[27]), ._12__Y4(Y[27]), ._11__A3(A[26]),
    ._10__B3(B[26]), ._9__Y3(Y[26]));  // open: _8__GND, _16__Vcc
endmodule

module _2_bit_RS (
  input  [24:0] S,
  input  Enable,
  output [24:0] out_3
);

  wire [24:0] Shifted;
  wire [27:0] bit_extender_1_out, bit_extender_2_out;
  wire [27:25] n28_bit_mux_1_y;

  assign bit_extender_1_out = {{3{1'b0}}, S};  // Bit_Extender bit_extender_1
  assign bit_extender_2_out = {{3{1'b0}}, Shifted};  // Bit_Extender bit_extender_2
  Shifter #(.width(25), .shift("lr")) shifter_1 (.in(S), .\dist (5'b00010), .out(Shifted));
  _28_Bit_MUX u_28_bit_mux_1 (.B(bit_extender_2_out), .Y({n28_bit_mux_1_y, out_3}), .A(bit_extender_1_out), .S(Enable));
endmodule

module _4_bit_RS (
  input  [24:0] S,
  input  Enable,
  output [24:0] out_3
);

  wire [24:0] Shifted;
  wire [27:0] bit_extender_1_out, bit_extender_2_out;
  wire [27:25] n28_bit_mux_1_y;

  assign bit_extender_1_out = {{3{1'b0}}, S};  // Bit_Extender bit_extender_1
  assign bit_extender_2_out = {{3{1'b0}}, Shifted};  // Bit_Extender bit_extender_2
  Shifter #(.width(25), .shift("lr")) shifter_1 (.in(S), .\dist (5'b00100), .out(Shifted));
  _28_Bit_MUX u_28_bit_mux_1 (.B(bit_extender_2_out), .Y({n28_bit_mux_1_y, out_3}), .A(bit_extender_1_out), .S(Enable));
endmodule

module _8_bit_RS (
  input  [24:0] S,
  input  Enable,
  output [24:0] out_3
);

  wire [24:0] Shifted;
  wire [27:0] bit_extender_1_out, bit_extender_2_out;
  wire [27:25] n28_bit_mux_1_y;

  assign bit_extender_1_out = {{3{1'b0}}, S};  // Bit_Extender bit_extender_1
  assign bit_extender_2_out = {{3{1'b0}}, Shifted};  // Bit_Extender bit_extender_2
  Shifter #(.width(25), .shift("lr")) shifter_1 (.in(S), .\dist (5'b01000), .out(Shifted));
  _28_Bit_MUX u_28_bit_mux_1 (.B(bit_extender_2_out), .Y({n28_bit_mux_1_y, out_3}), .A(bit_extender_1_out), .S(Enable));
endmodule

module _16_bit_RS (
  input  [24:0] S,
  input  Enable,
  output [24:0] out_3
);

  wire [24:0] Shifted;
  wire [27:0] bit_extender_1_out, bit_extender_2_out;
  wire [27:25] n28_bit_mux_1_y;

  assign bit_extender_1_out = {{3{1'b0}}, S};  // Bit_Extender bit_extender_1
  assign bit_extender_2_out = {{3{1'b0}}, Shifted};  // Bit_Extender bit_extender_2
  Shifter #(.width(25), .shift("lr")) shifter_1 (.in(S), .\dist (5'b10000), .out(Shifted));
  _28_Bit_MUX u_28_bit_mux_1 (.B(bit_extender_2_out), .Y({n28_bit_mux_1_y, out_3}), .A(bit_extender_1_out), .S(Enable));
endmodule

module Right_Shifter (
  input  [4:0] E,
  input  [24:0] A,
  output [24:0] Y
);

  wire [24:0] n2_bit_rs_1_out_3, n4_bit_rs_1_out_3, n8_bit_rs_1_out_3, n16_bit_rs_1_out_3;

  _16_bit_RS u_16_bit_rs_1 (.S(A), .out_3(n16_bit_rs_1_out_3), .Enable(E[4]));
  _8_bit_RS u_8_bit_rs_1 (.S(n16_bit_rs_1_out_3), .out_3(n8_bit_rs_1_out_3), .Enable(E[3]));
  _4_bit_RS u_4_bit_rs_1 (.S(n8_bit_rs_1_out_3), .out_3(n4_bit_rs_1_out_3), .Enable(E[2]));
  _2_bit_RS u_2_bit_rs_1 (.S(n4_bit_rs_1_out_3), .out_3(n2_bit_rs_1_out_3), .Enable(E[1]));
  _1_bit_RS u_1_bit_rs_1 (.Enable(E[0]), .S(n2_bit_rs_1_out_3), .out_3(Y));
endmodule

module _32_Bit_MUX (
  input  [31:0] B,
  input  [31:0] A,
  input  S,
  output [31:0] Y
);

  _74157 u_74157_1 (
    ._1__S(S), ._2__A1(A[0]), ._3__B1(B[0]), ._4__Y1(Y[0]), ._5__A2(A[1]), ._6__B2(B[1]), ._7__Y2(Y[1]),
    ._15__G(1'b0), ._14__A4(A[3]), ._13__B4(B[3]), ._12__Y4(Y[3]), ._11__A3(A[2]), ._10__B3(B[2]),
    ._9__Y3(Y[2]));  // open: _8__GND, _16__Vcc
  _28_Bit_MUX u_28_bit_mux_1 (.B(B[31:4]), .Y(Y[31:4]), .A(A[31:4]), .S(S));

  // Other names for the same wires on the sheet: A_4__28[27:0] = A[31:4]; B_4__28[27:0] = B[31:4];
  //   Y_4__28[27:0] = Y[31:4]
endmodule

module Re_arranger (
  input  [10:0] P,
  input  [10:0] Q,
  input  [31:0] A,
  input  [31:0] B,
  output [31:0] larger,
  output [31:0] smaller
);

  wire b_t;

  // Probe on A
  // Probe on B
  // Probe on P
  // Probe on Q
  _32_Bit_MUX u_32_bit_mux_1 (.B(B), .Y(larger), .A(A), .S(b_t));
  Subtractor #(.width(11)) subtractor_1 (.a(P), .b(Q), .bin(1'b0), .bout(b_t));  // open: out
  _32_Bit_MUX u_32_bit_mux_2 (.B(A), .Y(smaller), .A(B), .S(b_t));
  // Probe on larger
  // Probe on smaller
endmodule

module _1_bit_LS (
  input  [24:0] S,
  input  Enable,
  output [24:0] out_3
);

  wire [24:0] Shifted;
  wire [27:0] bit_extender_1_out, bit_extender_2_out;
  wire [27:25] n28_bit_mux_1_y;

  assign bit_extender_1_out = {{3{1'b0}}, S};  // Bit_Extender bit_extender_1
  assign bit_extender_2_out = {{3{1'b0}}, Shifted};  // Bit_Extender bit_extender_2
  Shifter #(.width(25)) shifter_1 (.in(S), .\dist (5'b00001), .out(Shifted));
  _28_Bit_MUX u_28_bit_mux_1 (.B(bit_extender_2_out), .Y({n28_bit_mux_1_y, out_3}), .A(bit_extender_1_out), .S(Enable));
endmodule

module _2_bit_LS (
  input  [24:0] S,
  input  Enable,
  output [24:0] out_3
);

  wire [24:0] Shifted;
  wire [27:0] bit_extender_1_out, bit_extender_2_out;
  wire [27:25] n28_bit_mux_1_y;

  assign bit_extender_1_out = {{3{1'b0}}, S};  // Bit_Extender bit_extender_1
  assign bit_extender_2_out = {{3{1'b0}}, Shifted};  // Bit_Extender bit_extender_2
  Shifter #(.width(25)) shifter_1 (.in(S), .\dist (5'b00010), .out(Shifted));
  _28_Bit_MUX u_28_bit_mux_1 (.B(bit_extender_2_out), .Y({n28_bit_mux_1_y, out_3}), .A(bit_extender_1_out), .S(Enable));
endmodule

module _4_bit_LS (
  input  [24:0] S,
  input  Enable,
  output [24:0] out_3
);

  wire [24:0] Shifted;
  wire [27:0] bit_extender_1_out, bit_extender_2_out;
  wire [27:25] n28_bit_mux_1_y;

  assign bit_extender_1_out = {{3{1'b0}}, S};  // Bit_Extender bit_extender_1
  assign bit_extender_2_out = {{3{1'b0}}, Shifted};  // Bit_Extender bit_extender_2
  Shifter #(.width(25)) shifter_1 (.in(S), .\dist (5'b00100), .out(Shifted));
  _28_Bit_MUX u_28_bit_mux_1 (.B(bit_extender_2_out), .Y({n28_bit_mux_1_y, out_3}), .A(bit_extender_1_out), .S(Enable));
endmodule

module _8_bit_LS (
  input  [24:0] S,
  input  Enable,
  output [24:0] out_3
);

  wire [24:0] Shifted;
  wire [27:0] bit_extender_1_out, bit_extender_2_out;
  wire [27:25] n28_bit_mux_1_y;

  assign bit_extender_1_out = {{3{1'b0}}, S};  // Bit_Extender bit_extender_1
  assign bit_extender_2_out = {{3{1'b0}}, Shifted};  // Bit_Extender bit_extender_2
  Shifter #(.width(25)) shifter_1 (.in(S), .\dist (5'b01000), .out(Shifted));
  _28_Bit_MUX u_28_bit_mux_1 (.B(bit_extender_2_out), .Y({n28_bit_mux_1_y, out_3}), .A(bit_extender_1_out), .S(Enable));
endmodule

module _16_bit_LS (
  input  [24:0] S,
  input  Enable,
  output [24:0] out_3
);

  wire [24:0] Shifted;
  wire [27:0] bit_extender_1_out, bit_extender_2_out;
  wire [27:25] n28_bit_mux_1_y;

  assign bit_extender_1_out = {{3{1'b0}}, S};  // Bit_Extender bit_extender_1
  assign bit_extender_2_out = {{3{1'b0}}, Shifted};  // Bit_Extender bit_extender_2
  Shifter #(.width(25)) shifter_1 (.in(S), .\dist (5'b10000), .out(Shifted));
  _28_Bit_MUX u_28_bit_mux_1 (.B(bit_extender_2_out), .Y({n28_bit_mux_1_y, out_3}), .A(bit_extender_1_out), .S(Enable));
endmodule

module Right_Shifter_Adapter (
  input  [10:0] S,
  output [4:0] E
);

  wire subtractor_1_bout;

  // Probe on S
  _7432 u_7432_1 (
    ._1__1A(S[4]), ._2__1B(subtractor_1_bout), ._3__1Y(E[4]), ._4__2A(S[3]), ._5__2B(subtractor_1_bout),
    ._6__2Y(E[3]), ._13__4B(subtractor_1_bout), ._12__4A(S[1]), ._11__4Y(E[1]), ._10__3B(subtractor_1_bout),
    ._9__3A(S[2]), ._8__3Y(E[2]));  // open: _7__GND, _14__Vcc
  Subtractor #(.width(11)) subtractor_1 (.a(11'h19), .b(S), .bin(1'b0), .bout(subtractor_1_bout));  // open: out
  _7432 u_7432_2 (
    ._1__1A(S[0]), ._2__1B(subtractor_1_bout), ._3__1Y(E[0]), ._5__2B(subtractor_1_bout),
    ._13__4B(subtractor_1_bout), ._10__3B(subtractor_1_bout));  // open: _4__2A, _6__2Y, _7__GND, _14__Vcc, _12__4A, _11__4Y, _9__3A, _8__3Y
endmodule

module Left_Shifter (
  input  [4:0] E,
  input  [24:0] A,
  output [24:0] Y
);

  wire [24:0] n2_bit_ls_1_out_3, n4_bit_ls_1_out_3, n8_bit_ls_1_out_3, n16_bit_ls_1_out_3;

  // Probe on A
  _16_bit_LS u_16_bit_ls_1 (.S(A), .out_3(n16_bit_ls_1_out_3), .Enable(E[4]));
  _8_bit_LS u_8_bit_ls_1 (.S(n16_bit_ls_1_out_3), .out_3(n8_bit_ls_1_out_3), .Enable(E[3]));
  _4_bit_LS u_4_bit_ls_1 (.S(n8_bit_ls_1_out_3), .out_3(n4_bit_ls_1_out_3), .Enable(E[2]));
  _2_bit_LS u_2_bit_ls_1 (.S(n4_bit_ls_1_out_3), .out_3(n2_bit_ls_1_out_3), .Enable(E[1]));
  // Probe on Y
  _1_bit_LS u_1_bit_ls_1 (.S(n2_bit_ls_1_out_3), .out_3(Y), .Enable(E[0]));
endmodule

module Right_Shift_Wrapper (
  input  [23:0] A,
  input  [10:0] S,
  output [23:0] Y
);

  wire [4:0] right_shifter_adapter_1_e;
  wire [24:0] bit_extender_1_out;
  wire [24:24] right_shifter_1_y;

  assign bit_extender_1_out = {{1{1'b0}}, A};  // Bit_Extender bit_extender_1
  // Probe on S
  // Probe on bit_extender_1_out
  Right_Shifter_Adapter right_shifter_adapter_1 (.S(S), .E(right_shifter_adapter_1_e));
  Right_Shifter right_shifter_1 (.A(bit_extender_1_out), .E(right_shifter_adapter_1_e), .Y({right_shifter_1_y[24], Y}));
  // Probe on Y
endmodule

module Rounder (
  input  [22:0] S,
  input  [10:0] Exponent,
  output [19:0] R,
  output [10:0] RoundedExponent,
  output RoundingOverflow
);

  wire adder_1_cout, adder_2_cout, n7408_1__3__1y, n7432_1__3__1y, n7432_1__8__3y;
  wire [10:0] bit_extender_2_out;
  wire [19:0] bit_extender_1_out;

  _7432 u_7432_1 (
    ._1__1A(S[1]), ._2__1B(S[0]), ._3__1Y(n7432_1__3__1y), ._10__3B(S[3]), ._9__3A(n7432_1__3__1y),
    ._8__3Y(n7432_1__8__3y));  // open: _4__2A, _5__2B, _6__2Y, _7__GND, _14__Vcc, _13__4B, _12__4A, _11__4Y
  Adder #(.width(20)) adder_1 (.a(S[22:3]), .b(bit_extender_1_out), .out(R), .cin(n7408_1__3__1y), .cout(adder_1_cout));
  assign bit_extender_1_out = {{19{1'b0}}, 1'b0};  // Bit_Extender bit_extender_1
  _7408 u_7408_1 (
    ._1__1A(S[2]), ._2__1B(n7432_1__8__3y), ._3__1Y(n7408_1__3__1y));  // open: _4__2A, _5__2B, _6__2Y, _7__GND, _14__Vcc, _13__4B, _12__4A, _11__4Y, _10__3B, _9__3A, _8__3Y
  assign bit_extender_2_out = {{10{1'b0}}, 1'b0};  // Bit_Extender bit_extender_2
  Adder #(.width(11)) adder_2 (
    .a(Exponent), .b(bit_extender_2_out), .out(RoundedExponent), .cin(adder_1_cout), .cout(adder_2_cout));
  Overflow_Detector overflow_detector_1 (.Carry(adder_2_cout), .Exponent(RoundedExponent), .Overflow(RoundingOverflow));

  // Other names for the same wires on the sheet: Sticky = S[0]; Round = S[1]; Guard = S[2]; S0 = S[3];
  //   S_t[19:0] = S[22:3]
endmodule

module _74148 (
  input  _1__I4,
  input  _16__Vcc,
  input  _2__I5,
  input  _3__I6,
  input  _4__I7,
  input  _13__I3,
  input  _5__EI,
  input  _12__I2,
  input  _11__I1,
  input  _10__I0,
  input  _8__GND,
  output _15__EO,
  output _16__GS,
  output _6__A2,
  output _7__A1,
  output _9__A0
);

  wire not_1_out, not_2_out, not_3_out, not_4_out, not_5_out, not_6_out, not_7_out, not_8_out, not_9_out,
       not_10_out, not_11_out, not_12_out, priority_encoder_1_en_out, priority_encoder_1_gs;
  wire [2:0] priority_encoder_1_out;

  or or_1 (_16__GS, priority_encoder_1_en_out, _5__EI);
  not not_1 (not_1_out, _10__I0);
  not not_2 (not_2_out, _11__I1);
  not not_3 (not_3_out, _12__I2);
  Priority_Encoder #(.disabled(0)) priority_encoder_1 (
    .in0(not_1_out), .in1(not_2_out), .in2(not_3_out), .in3(not_4_out), .in4(not_5_out), .in5(not_6_out),
    .in6(not_7_out), .in7(not_8_out), .out(priority_encoder_1_out), .en_in(not_9_out),
    .gs(priority_encoder_1_gs), .en_out(priority_encoder_1_en_out));
  not not_4 (not_4_out, _13__I3);
  not not_5 (not_5_out, _1__I4);
  not not_6 (not_6_out, _2__I5);
  not not_7 (not_7_out, _3__I6);
  not not_8 (not_8_out, _4__I7);
  not not_9 (not_9_out, _5__EI);
  or or_2 (_15__EO, priority_encoder_1_gs, _5__EI);
  not not_10 (not_10_out, priority_encoder_1_out[0]);
  not not_11 (not_11_out, priority_encoder_1_out[1]);
  not not_12 (not_12_out, priority_encoder_1_out[2]);
  or or_3 (_9__A0, not_10_out, _16__GS);
  or or_4 (_7__A1, not_11_out, _16__GS);
  or or_5 (_6__A2, not_12_out, _16__GS);

  // Other names for the same wires on the sheet: A0 = _9__A0; A1 = _7__A1; A2 = _6__A2; E = _5__EI; EO = _15__EO;
  //   GS = _16__GS; I0 = _10__I0; I1 = _11__I1; I2 = _12__I2; I3 = _13__I3; I4 = _1__I4; I5 = _2__I5; I6 = _3__I6;
  //   I7 = _4__I7

  // Notes on the sheet:
  //   _8__GND: pull=down
  //   _16__Vcc: pull=up
  //   74148: 8-Line to 4-Line Priority Encoder
endmodule

module Overflow_Detector (
  input  [10:0] Exponent,
  input  Carry,
  output Overflow
);

  Subtractor #(.width(12)) subtractor_1 (.a(12'h7fe), .b({Carry, Exponent}), .bout(Overflow));  // open: out, bin
endmodule

module Normalizer (
  input  [24:0] Significand,
  input  [10:0] Exponent,
  output [22:0] Normal_Significand,
  output [10:0] Normal_Exponent,
  output Normalizing_Overflow
);

  wire Carry, E0, E1, E2, E3, E4, E8, n7402_1__1__1y, n7432_1__3__1y, n7432_2__3__1y, n7432_2__6__2y,
       n7432_2__8__3y, n7432_2__11__4y, n7432_3__3__1y, n7432_3__6__2y;
  wire [4:0] bit_extender_1_out, LeftShiftAmount, n5_bit_mux_1_y;
  wire [5:5] n32_bit_input_high_encoder_1_o;
  wire [10:0] ModifiedExponent;
  wire [24:0] bit_extender_2_out, bit_extender_3_out, n1_bit_rs_1_out_3;
  wire [24:23] left_shifter_1_y;
  wire [25:12] asu_1_y;

  _7432 u_7432_1 (
    ._1__1A(Significand[23]), ._2__1B(Significand[24]), ._3__1Y(n7432_1__3__1y));  // open: _4__2A, _5__2B, _6__2Y, _7__GND, _14__Vcc, _13__4B, _12__4A, _11__4Y, _10__3B, _9__3A, _8__3Y
  _7432 u_7432_2 (
    ._1__1A(Significand[24]), ._2__1B(LeftShiftAmount[0]), ._3__1Y(n7432_2__3__1y), ._4__2A(n7432_2__3__1y),
    ._5__2B(LeftShiftAmount[1]), ._6__2Y(n7432_2__6__2y), ._13__4B(LeftShiftAmount[2]),
    ._12__4A(n7432_2__8__3y), ._11__4Y(n7432_2__11__4y), ._10__3B(LeftShiftAmount[3]),
    ._9__3A(n7432_2__6__2y), ._8__3Y(n7432_2__8__3y));  // open: _7__GND, _14__Vcc
  _1_bit_RS u_1_bit_rs_1 (.Enable(Significand[24]), .S(Significand), .out_3(n1_bit_rs_1_out_3));
  assign bit_extender_1_out = {{4{1'b0}}, Significand[24]};  // Bit_Extender bit_extender_1
  _32_bit_input_high_encoder u_32_bit_input_high_encoder_1 (
    .I({Significand[22:0], {9{1'b0}}}), ._1_based_indexing(1'b1),
    .O({n32_bit_input_high_encoder_1_o[5], LeftShiftAmount}));
  Left_Shifter left_shifter_1 (
    .A(n1_bit_rs_1_out_3), .E({E4, E3, E2, E1, E0}), .Y({left_shifter_1_y, Normal_Significand}));
  _5_Bit_MUX u_5_bit_mux_1 (.Y(n5_bit_mux_1_y), .B(bit_extender_1_out), .A(LeftShiftAmount), .S(n7432_1__3__1y));
  _7432 u_7432_3 (
    ._1__1A(LeftShiftAmount[4]), ._2__1B(n7432_2__11__4y), ._3__1Y(n7432_3__3__1y), ._4__2A(n7432_3__3__1y),
    ._5__2B(Significand[23]), ._6__2Y(n7432_3__6__2y));  // open: _7__GND, _14__Vcc, _13__4B, _12__4A, _11__4Y, _10__3B, _9__3A, _8__3Y
  _7408 u_7408_1 (
    ._1__1A(n7432_3__6__2y), ._2__1B(E8), ._3__1Y(Carry));  // open: _4__2A, _5__2B, _6__2Y, _7__GND, _14__Vcc, _13__4B, _12__4A, _11__4Y, _10__3B, _9__3A, _8__3Y
  assign bit_extender_2_out = {{20{1'b0}}, n5_bit_mux_1_y};  // Bit_Extender bit_extender_2
  assign bit_extender_3_out = {{14{1'b0}}, Exponent};  // Bit_Extender bit_extender_3
  _7402 u_7402_1 (
    ._1__1Y(n7402_1__1__1y), ._2__1A(Significand[23]), ._3__1B(Significand[24]));  // open: _4__2Y, _5__2A, _6__2B, _7__GND, _14__Vcc, _13__4Y, _12__4B, _11__4A, _10__3Y, _9__3B, _8__3A
  ASU asu_1 (
    .B_Cin(1'b0), .A(bit_extender_3_out), .B(bit_extender_2_out), .Y({asu_1_y, E8, ModifiedExponent}),
    .Add(n7432_1__3__1y));
  _11_bit_MUX u_11_bit_mux_1 (.B(ModifiedExponent), .Y(Normal_Exponent), .A({11{1'b0}}), .S(n7432_3__6__2y));
  _7408 u_7408_2 (
    ._1__1A(n7402_1__1__1y), ._2__1B(LeftShiftAmount[4]), ._3__1Y(E4), ._4__2A(n7402_1__1__1y),
    ._5__2B(LeftShiftAmount[3]), ._6__2Y(E3), ._13__4B(n7402_1__1__1y), ._12__4A(LeftShiftAmount[2]),
    ._11__4Y(E2), ._10__3B(n7402_1__1__1y), ._9__3A(LeftShiftAmount[1]), ._8__3Y(E1));  // open: _7__GND, _14__Vcc
  Overflow_Detector overflow_detector_1 (.Carry(Carry), .Exponent(Normal_Exponent), .Overflow(Normalizing_Overflow));
  _7408 u_7408_3 (
    ._1__1A(n7402_1__1__1y), ._2__1B(LeftShiftAmount[0]), ._3__1Y(E0));  // open: _4__2A, _5__2B, _6__2Y, _7__GND, _14__Vcc, _13__4B, _12__4A, _11__4Y, _10__3B, _9__3A, _8__3Y

  // Other names for the same wires on the sheet: O0 = LeftShiftAmount[0]; O1 = LeftShiftAmount[1];
  //   O2 = LeftShiftAmount[2]; O3 = LeftShiftAmount[3]; O4 = LeftShiftAmount[4]; S26 = Significand[23];
  //   S27 = Significand[24]
endmodule

module _5_Bit_MUX (
  input  [4:0] B,
  input  [4:0] A,
  input  S,
  output [4:0] Y
);

  _74157 u_74157_1 (
    ._1__S(S), ._2__A1(A[0]), ._3__B1(B[0]), ._4__Y1(Y[0]), ._5__A2(A[1]), ._6__B2(B[1]), ._7__Y2(Y[1]),
    ._15__G(1'b0), ._14__A4(A[3]), ._13__B4(B[3]), ._12__Y4(Y[3]), ._11__A3(A[2]), ._10__B3(B[2]),
    ._9__Y3(Y[2]));  // open: _8__GND, _16__Vcc
  _74157 u_74157_2 (
    ._1__S(S), ._2__A1(A[4]), ._3__B1(B[4]), ._4__Y1(Y[4]), ._15__G(1'b0));  // open: _5__A2, _6__B2, _7__Y2, _8__GND, _16__Vcc, _14__A4, _13__B4, _12__Y4, _11__A3, _10__B3, _9__Y3
endmodule

module _8_Bit_MUX (
  input  [7:0] A,
  input  [7:0] B,
  input  S,
  output [7:0] Y
);

  _74157 u_74157_1 (
    ._1__S(S), ._2__A1(A[0]), ._3__B1(B[0]), ._4__Y1(Y[0]), ._5__A2(A[1]), ._6__B2(B[1]), ._7__Y2(Y[1]),
    ._15__G(1'b0), ._14__A4(A[3]), ._13__B4(B[3]), ._12__Y4(Y[3]), ._11__A3(A[2]), ._10__B3(B[2]),
    ._9__Y3(Y[2]));  // open: _8__GND, _16__Vcc
  _74157 u_74157_2 (
    ._1__S(S), ._2__A1(A[4]), ._3__B1(B[4]), ._4__Y1(Y[4]), ._5__A2(A[5]), ._6__B2(B[5]), ._7__Y2(Y[5]),
    ._15__G(1'b0), ._14__A4(A[7]), ._13__B4(B[7]), ._12__Y4(Y[7]), ._11__A3(A[6]), ._10__B3(B[6]),
    ._9__Y3(Y[6]));  // open: _8__GND, _16__Vcc
endmodule

module Floating_Point_Adder (
  input  [31:0] A,
  input  [31:0] B,
  output [31:0] Y,
  output Overflow
);

  wire A_pre_decimal, B_pre_decimal, n7486_1__3__1y, NormalizationOverflow, RoundingOverflow, SameSign;
  wire [7:0] NormalExponent;
  wire [10:0] exponent_difference, larger_exponent, smaller_exponent;
  wire [22:3] padded_significand_2_prime;
  wire [22:20] RoundedSignificand, significand_of_larger_exp, significand_of_smaller_exp;
  wire [23:0] n24_bit_mux_1_y, n24_bit_mux_2_y, padded_significand_2;
  wire [24:0] ASUInput1, ASUInput2;
  wire [25:0] NormalSignificand;
  wire [27:0] AddedSignificand;
  wire [28:0] ASUOutput;
  wire [31:0] larger_exponent_float;
  wire [31:31] smaller_exponent_float;

  Subtractor #(.width(11)) subtractor_1 (
    .a(larger_exponent), .b(smaller_exponent), .out(exponent_difference), .bin(1'b0));  // open: bout
  Right_Shift_Wrapper right_shift_wrapper_1 (
    .A({B_pre_decimal, padded_significand_2_prime, 3'b000}), .S(exponent_difference), .Y(padded_significand_2));
  _7404 u_7404_1 (
    ._13__6A(n7486_1__3__1y), ._12__6Y(SameSign));  // open: _1__1A, _2__1Y, _3__2A, _4__2Y, _5__3A, _6__3Y, _7__GND, _14__Vcc, _11__5A, _10__5Y, _9__4A, _8__4Y
  _7486 u_7486_1 (
    ._1__1A(A[31]), ._2__1B(B[31]), ._3__1Y(n7486_1__3__1y));  // open: _4__2A, _5__2B, _6__2Y, _7__GND, _14__Vcc, _13__4B, _12__4A, _11__4Y, _10__3B, _9__3A, _8__3Y
  ZeroChecker zerochecker_1 (.A(A), .NotZero(A_pre_decimal));
  // Normalizer normalizer_1: pin names not known; wires that end beside it: AddedSignificand, larger_exponent, NormalSignificand, NormalExponent, NormalizationOverflow
  // Rounder rounder_1: pin names not known; wires that end beside it: NormalSignificand, NormalExponent, {RoundedSignificand, Y[19:0]}, Y[30:20], RoundingOverflow
  Re_arranger re_arranger_1 (
    .P(A[30:20]), .Q(B[30:20]), .A(A), .B(B),
    .larger({larger_exponent_float[31], larger_exponent, larger_exponent_float[19:0]}),
    .smaller({smaller_exponent_float[31], smaller_exponent, padded_significand_2_prime}));
  ZeroChecker zerochecker_2 (.A(B), .NotZero(B_pre_decimal));
  // ABS abs_1: pin names not known; wires that end beside it: ASUOutput, AddedSignificand
  ASU asu_1 (.B_Cin(1'b0), .A(ASUInput1), .B(ASUInput2), .Y(ASUOutput[25:0]), .Add(SameSign));
  _24_bit_MUX u_24_bit_mux_1 (
    .B(padded_significand_2), .Y(n24_bit_mux_1_y), .A({A_pre_decimal, larger_exponent_float[19:0], 3'b000}),
    .S(larger_exponent_float[31]));
  _24_bit_MUX u_24_bit_mux_2 (
    .B({A_pre_decimal, larger_exponent_float[19:0], 3'b000}), .Y(n24_bit_mux_2_y), .A(padded_significand_2),
    .S(larger_exponent_float[31]));
  _7432 u_7432_1 (
    ._1__1A(NormalizationOverflow), ._2__1B(RoundingOverflow), ._3__1Y(Overflow));  // open: _4__2A, _5__2B, _6__2Y, _7__GND, _14__Vcc, _13__4B, _12__4A, _11__4Y, _10__3B, _9__3A, _8__3Y
  _74157 u_74157_1 (
    ._1__S(SameSign), ._2__A1(ASUOutput[27]), ._3__B1(A[31]), ._4__Y1(Y[31]), ._15__G(1'b0));  // open: _5__A2, _6__B2, _7__Y2, _8__GND, _16__Vcc, _14__A4, _13__B4, _12__Y4, _11__A3, _10__B3, _9__Y3
  assign ASUInput1 = {{1{1'b0}}, n24_bit_mux_1_y};  // Bit_Extender bit_extender_1
  assign ASUInput2 = {{1{1'b0}}, n24_bit_mux_2_y};  // Bit_Extender bit_extender_2
  // Pins of 20 and 23 bits meet at {significand_of_smaller_exp, padded_significand_2_prime}
  // Pins of 8 and 11 bits meet at Y[30:20]
  // Pins of 8 and 11 bits meet at larger_exponent
  // Pins of 25 and 26 and 29 bits meet at ASUOutput
  // Pins of 20 and 23 bits meet at {RoundedSignificand, Y[19:0]}
  // Pins of 20 and 23 bits meet at {significand_of_larger_exp, larger_exponent_float[19:0]}

  // Other names for the same wires on the sheet: Significand_A[19:0] = A[19:0]; Exponent_A[10:0] = A[30:20];
  //   Sign_A = A[31]; SumSign = ASUOutput[27]; Significand_B[19:0] = B[19:0]; Exponent_B[10:0] = B[30:20];
  //   Sign_B = B[31]; larger_exponent_float[30:20] = larger_exponent; RearrangedSign1 = larger_exponent_float[31];
  //   padded_significand_1[23:3] = {A_pre_decimal, larger_exponent_float[19:0]};
  //   significand_of_larger_exp[19:0] = larger_exponent_float[19:0];
  //   significand_of_smaller_exp[19:0] = padded_significand_2_prime;
  //   smaller_exponent_float[30:0] = {smaller_exponent, padded_significand_2_prime};
  //   padded_significand_2_prime[23] = B_pre_decimal; RoundedSignificand[19:0] = Y[19:0];
  //   RoundedExponent[10:0] = Y[30:20]; Sign = Y[31]
endmodule

module ZeroChecker (
  input  [31:0] A,
  output NotZero
);

  wire n7432_1__3__1y, n7432_1__6__2y, n7432_1__8__3y, n7432_1__11__4y, n7432_2__3__1y, n7432_2__6__2y,
       n7432_2__8__3y, n7432_2__11__4y, n7432_3__3__1y, n7432_3__6__2y, n7432_3__8__3y, n7432_3__11__4y,
       n7432_4__3__1y, n7432_4__6__2y, n7432_4__8__3y, n7432_4__11__4y, n7432_5__3__1y, n7432_5__6__2y,
       n7432_5__8__3y, n7432_5__11__4y, n7432_6__3__1y, n7432_6__6__2y, n7432_6__8__3y, n7432_6__11__4y,
       n7432_7__3__1y, n7432_7__6__2y, n7432_7__8__3y, n7432_7__11__4y, n7432_8__3__1y, n7432_8__6__2y,
       undriven;

  _7432 u_7432_1 (
    ._1__1A(A[0]), ._2__1B(A[1]), ._3__1Y(n7432_1__3__1y), ._4__2A(n7432_1__3__1y), ._5__2B(A[2]),
    ._6__2Y(n7432_1__6__2y), ._13__4B(A[3]), ._12__4A(n7432_1__8__3y), ._11__4Y(n7432_1__11__4y),
    ._10__3B(A[4]), ._9__3A(n7432_1__6__2y), ._8__3Y(n7432_1__8__3y));  // open: _7__GND, _14__Vcc
  _7432 u_7432_2 (
    ._1__1A(n7432_1__11__4y), ._2__1B(A[5]), ._3__1Y(n7432_2__3__1y), ._4__2A(n7432_2__3__1y), ._5__2B(A[6]),
    ._6__2Y(n7432_2__6__2y), ._13__4B(A[7]), ._12__4A(n7432_2__8__3y), ._11__4Y(n7432_2__11__4y),
    ._10__3B(A[8]), ._9__3A(n7432_2__6__2y), ._8__3Y(n7432_2__8__3y));  // open: _7__GND, _14__Vcc
  _7432 u_7432_3 (
    ._1__1A(n7432_2__11__4y), ._2__1B(A[9]), ._3__1Y(n7432_3__3__1y), ._4__2A(n7432_3__3__1y),
    ._5__2B(A[10]), ._6__2Y(n7432_3__6__2y), ._13__4B(A[11]), ._12__4A(n7432_3__8__3y),
    ._11__4Y(n7432_3__11__4y), ._10__3B(A[12]), ._9__3A(n7432_3__6__2y), ._8__3Y(n7432_3__8__3y));  // open: _7__GND, _14__Vcc
  _7432 u_7432_4 (
    ._1__1A(n7432_3__11__4y), ._2__1B(A[13]), ._3__1Y(n7432_4__3__1y), ._4__2A(n7432_4__3__1y),
    ._5__2B(A[14]), ._6__2Y(n7432_4__6__2y), ._13__4B(A[15]), ._12__4A(n7432_4__8__3y),
    ._11__4Y(n7432_4__11__4y), ._10__3B(A[16]), ._9__3A(n7432_4__6__2y), ._8__3Y(n7432_4__8__3y));  // open: _7__GND, _14__Vcc
  _7432 u_7432_5 (
    ._1__1A(n7432_4__11__4y), ._2__1B(A[17]), ._3__1Y(n7432_5__3__1y), ._4__2A(n7432_5__3__1y),
    ._5__2B(A[18]), ._6__2Y(n7432_5__6__2y), ._13__4B(A[19]), ._12__4A(n7432_5__8__3y),
    ._11__4Y(n7432_5__11__4y), ._10__3B(A[20]), ._9__3A(n7432_5__6__2y), ._8__3Y(n7432_5__8__3y));  // open: _7__GND, _14__Vcc
  _7432 u_7432_6 (
    ._1__1A(n7432_5__11__4y), ._2__1B(A[21]), ._3__1Y(n7432_6__3__1y), ._4__2A(n7432_6__3__1y),
    ._5__2B(A[22]), ._6__2Y(n7432_6__6__2y), ._13__4B(A[23]), ._12__4A(n7432_6__8__3y),
    ._11__4Y(n7432_6__11__4y), ._10__3B(A[24]), ._9__3A(n7432_6__6__2y), ._8__3Y(n7432_6__8__3y));  // open: _7__GND, _14__Vcc
  _7432 u_7432_7 (
    ._1__1A(n7432_6__11__4y), ._2__1B(A[25]), ._3__1Y(n7432_7__3__1y), ._4__2A(n7432_7__3__1y),
    ._5__2B(A[26]), ._6__2Y(n7432_7__6__2y), ._13__4B(A[27]), ._12__4A(n7432_7__8__3y),
    ._11__4Y(n7432_7__11__4y), ._10__3B(A[28]), ._9__3A(n7432_7__6__2y), ._8__3Y(n7432_7__8__3y));  // open: _7__GND, _14__Vcc
  _7432 u_7432_8 (
    ._1__1A(n7432_7__11__4y), ._2__1B(A[29]), ._3__1Y(n7432_8__3__1y), ._4__2A(n7432_8__3__1y),
    ._5__2B(A[30]), ._6__2Y(n7432_8__6__2y), ._13__4B(undriven), ._10__3B(A[31]), ._9__3A(n7432_8__6__2y),
    ._8__3Y(NotZero));  // open: _7__GND, _14__Vcc, _12__4A, _11__4Y
endmodule

module _16_bit_priority_encoder (
  input  [15:0] I,
  input  EI,
  output [3:0] O,
  output EO,
  output GS
);

  wire A0_0, A0_1, A1_0, A1_1, A2_0, A2_1, GS_0, n74148_1__15__eo;

  _74148 u_74148_1 (
    ._1__I4(I[12]), ._2__I5(I[13]), ._3__I6(I[14]), ._4__I7(I[15]), ._5__EI(EI), ._6__A2(A2_1),
    ._7__A1(A1_1), ._15__EO(n74148_1__15__eo), ._16__GS(O[3]), ._13__I3(I[11]), ._12__I2(I[10]),
    ._11__I1(I[9]), ._10__I0(I[8]), ._9__A0(A0_1));  // open: _8__GND, _16__Vcc
  _74148 u_74148_2 (
    ._1__I4(I[4]), ._2__I5(I[5]), ._3__I6(I[6]), ._4__I7(I[7]), ._5__EI(n74148_1__15__eo), ._6__A2(A2_0),
    ._7__A1(A1_0), ._15__EO(EO), ._16__GS(GS_0), ._13__I3(I[3]), ._12__I2(I[2]), ._11__I1(I[1]),
    ._10__I0(I[0]), ._9__A0(A0_0));  // open: _8__GND, _16__Vcc
  _7408 u_7408_1 (
    ._1__1A(A2_1), ._2__1B(A2_0), ._3__1Y(O[2]), ._4__2A(A1_1), ._5__2B(A1_0), ._6__2Y(O[1]), ._13__4B(A0_1),
    ._12__4A(A0_0), ._11__4Y(O[0]), ._10__3B(GS_0), ._9__3A(O[3]), ._8__3Y(GS));  // open: _7__GND, _14__Vcc

  // Other names for the same wires on the sheet: A0 = O[0]; A1 = O[1]; A2 = O[2]; A3 = O[3]
endmodule

module _32_bit_encoder (
  input  EI,
  input  [31:0] I,
  output [4:0] O
);

  wire n16_bit_priority_encoder_1_eo, O0_0, O0_1, O1_0, O1_1, O2_0, O2_1, O3_0, O3_1;

  _16_bit_priority_encoder u_16_bit_priority_encoder_1 (
    .EI(EI), .EO(n16_bit_priority_encoder_1_eo), .GS(O[4]), .I(I[31:16]), .O({O3_1, O2_1, O1_1, O0_1}));
  _16_bit_priority_encoder u_16_bit_priority_encoder_2 (
    .EI(n16_bit_priority_encoder_1_eo), .I(I[15:0]), .O({O3_0, O2_0, O1_0, O0_0}));  // open: EO, GS
  _7408 u_7408_1 (
    ._1__1A(O2_1), ._2__1B(O2_0), ._3__1Y(O[2]), ._4__2A(O1_1), ._5__2B(O1_0), ._6__2Y(O[1]), ._13__4B(O0_1),
    ._12__4A(O0_0), ._11__4Y(O[0]), ._10__3B(O3_1), ._9__3A(O3_0), ._8__3Y(O[3]));  // open: _7__GND, _14__Vcc

  // Other names for the same wires on the sheet: I0[15:0] = I[15:0]; I1[15:0] = I[31:16];
  //   O_0[3:0] = {O3_0, O2_0, O1_0, O0_0}; O_1[3:0] = {O3_1, O2_1, O1_1, O0_1}
endmodule

module _32_bit_input_high_encoder (
  input  [31:0] I,
  input  _1_based_indexing,
  output [5:0] O
);

  wire I0_prime, I1_prime, I2_prime, I3_prime, I4_prime, I5_prime, I6_prime, I7_prime, I8_prime, I9_prime,
       I10_prime, I11_prime, I12_prime, I13_prime, I14_prime, I15_prime, I16_prime, I17_prime, I18_prime,
       I19_prime, I20_prime, I21_prime, I22_prime, I23_prime, I24_prime, I25_prime, I26_prime, I27_prime,
       I28_prime, I29_prime, I30_prime, I31_prime;
  wire [4:0] bit_extender_1_out, n32_bit_encoder_1_o;

  _7404 u_7404_1 (
    ._1__1A(I[0]), ._2__1Y(I0_prime), ._3__2A(I[1]), ._4__2Y(I1_prime), ._5__3A(I[2]), ._6__3Y(I2_prime),
    ._13__6A(I[3]), ._12__6Y(I3_prime), ._11__5A(I[4]), ._10__5Y(I4_prime), ._9__4A(I[5]), ._8__4Y(I5_prime));  // open: _7__GND, _14__Vcc
  _7404 u_7404_2 (
    ._1__1A(I[6]), ._2__1Y(I6_prime), ._3__2A(I[7]), ._4__2Y(I7_prime), ._5__3A(I[8]), ._6__3Y(I8_prime),
    ._13__6A(I[9]), ._12__6Y(I9_prime), ._11__5A(I[10]), ._10__5Y(I10_prime), ._9__4A(I[11]),
    ._8__4Y(I11_prime));  // open: _7__GND, _14__Vcc
  _7404 u_7404_3 (
    ._1__1A(I[12]), ._2__1Y(I12_prime), ._3__2A(I[13]), ._4__2Y(I13_prime), ._5__3A(I[14]),
    ._6__3Y(I14_prime), ._13__6A(I[15]), ._12__6Y(I15_prime), ._11__5A(I[16]), ._10__5Y(I16_prime),
    ._9__4A(I[17]), ._8__4Y(I17_prime));  // open: _7__GND, _14__Vcc
  _7404 u_7404_4 (
    ._1__1A(I[18]), ._2__1Y(I18_prime), ._3__2A(I[19]), ._4__2Y(I19_prime), ._5__3A(I[20]),
    ._6__3Y(I20_prime), ._13__6A(I[21]), ._12__6Y(I21_prime), ._11__5A(I[22]), ._10__5Y(I22_prime),
    ._9__4A(I[23]), ._8__4Y(I23_prime));  // open: _7__GND, _14__Vcc
  _7404 u_7404_5 (
    ._1__1A(I[24]), ._2__1Y(I24_prime), ._3__2A(I[25]), ._4__2Y(I25_prime), ._5__3A(I[26]),
    ._6__3Y(I26_prime), ._13__6A(I[27]), ._12__6Y(I27_prime), ._11__5A(I[28]), ._10__5Y(I28_prime),
    ._9__4A(I[29]), ._8__4Y(I29_prime));  // open: _7__GND, _14__Vcc
  _7404 u_7404_6 (
    ._1__1A(I[30]), ._2__1Y(I30_prime), ._3__2A(I[31]), ._4__2Y(I31_prime));  // open: _5__3A, _6__3Y, _7__GND, _14__Vcc, _13__6A, _12__6Y, _11__5A, _10__5Y, _9__4A, _8__4Y
  _32_bit_encoder u_32_bit_encoder_1 (
    .EI(1'b0),
    .I({I31_prime, I30_prime, I29_prime, I28_prime, I27_prime, I26_prime, I25_prime, I24_prime, I23_prime, I22_prime, I21_prime, I20_prime, I19_prime, I18_prime, I17_prime, I16_prime, I15_prime, I14_prime, I13_prime, I12_prime, I11_prime, I10_prime, I9_prime, I8_prime, I7_prime, I6_prime, I5_prime, I4_prime, I3_prime, I2_prime, I1_prime, I0_prime}),
    .O(n32_bit_encoder_1_o));
  assign bit_extender_1_out = {{4{1'b0}}, 1'b0};  // Bit_Extender bit_extender_1
  Adder #(.width(5)) adder_1 (
    .a(n32_bit_encoder_1_o), .b(bit_extender_1_out), .out(O[4:0]), .cin(_1_based_indexing), .cout(O[5]));

  // Other names for the same wires on the sheet: I_prime[31:0] = {I31_prime, I30_prime, I29_prime, I28_prime, I27_prime, I26_prime, I25_prime, I24_prime, I23_prime, I22_prime, I21_prime, I20_prime, I19_prime, I18_prime, I17_prime, I16_prime, I15_prime, I14_prime, I13_prime, I12_prime, I11_prime, I10_prime, I9_prime, I8_prime, I7_prime, I6_prime, I5_prime, I4_prime, I3_prime, I2_prime, I1_prime, I0_prime}
endmodule

module ASU (
  input  B_Cin,
  input  Add,
  input  [24:0] A,
  input  [24:0] B,
  output [25:0] Y
);

  wire bout, cout;
  wire [24:0] Add_t, Sub;

  // Probe on B
  // Probe on A
  Adder #(.width(25)) adder_1 (.a(A), .b(B), .out(Add_t), .cin(B_Cin), .cout(cout));
  Subtractor #(.width(25)) subtractor_1 (.a(A), .b(B), .out(Sub), .bin(B_Cin), .bout(bout));
  _74157 u_74157_1 (
    ._1__S(Add), ._2__A1(bout), ._3__B1(cout), ._4__Y1(Y[25]), ._15__G(1'b0));  // open: _5__A2, _6__B2, _7__Y2, _8__GND, _16__Vcc, _14__A4, _13__B4, _12__Y4, _11__A3, _10__B3, _9__Y3
  Multiplexer #(.width(25), .enable("false")) multiplexer_1 (.in0(Sub), .in1(Add_t), .out(Y[24:0]), .sel(Add));
  // Probe on Y
endmodule

module ABS (
  input  [25:0] A,
  output [24:0] ABS
);

  wire [24:0] _1_s_Comp, bit_extender_1_out;

  _7486 u_7486_1 (
    ._1__1A(A[0]), ._2__1B(A[25]), ._3__1Y(_1_s_Comp[0]), ._4__2A(A[1]), ._5__2B(A[25]),
    ._6__2Y(_1_s_Comp[1]), ._13__4B(A[25]), ._12__4A(A[3]), ._11__4Y(_1_s_Comp[3]), ._10__3B(A[25]),
    ._9__3A(A[2]), ._8__3Y(_1_s_Comp[2]));  // open: _7__GND, _14__Vcc
  _7486 u_7486_2 (
    ._1__1A(A[16]), ._2__1B(A[25]), ._3__1Y(_1_s_Comp[16]), ._4__2A(A[17]), ._5__2B(A[25]),
    ._6__2Y(_1_s_Comp[17]), ._13__4B(A[25]), ._12__4A(A[19]), ._11__4Y(_1_s_Comp[19]), ._10__3B(A[25]),
    ._9__3A(A[18]), ._8__3Y(_1_s_Comp[18]));  // open: _7__GND, _14__Vcc
  // Probe on A
  _7486 u_7486_3 (
    ._1__1A(A[4]), ._2__1B(A[25]), ._3__1Y(_1_s_Comp[4]), ._4__2A(A[5]), ._5__2B(A[25]),
    ._6__2Y(_1_s_Comp[5]), ._13__4B(A[25]), ._12__4A(A[7]), ._11__4Y(_1_s_Comp[7]), ._10__3B(A[25]),
    ._9__3A(A[6]), ._8__3Y(_1_s_Comp[6]));  // open: _7__GND, _14__Vcc
  _7486 u_7486_4 (
    ._1__1A(A[20]), ._2__1B(A[25]), ._3__1Y(_1_s_Comp[20]), ._4__2A(A[21]), ._5__2B(A[25]),
    ._6__2Y(_1_s_Comp[21]), ._13__4B(A[25]), ._12__4A(A[23]), ._11__4Y(_1_s_Comp[23]), ._10__3B(A[25]),
    ._9__3A(A[22]), ._8__3Y(_1_s_Comp[22]));  // open: _7__GND, _14__Vcc
  _7486 u_7486_5 (
    ._1__1A(A[8]), ._2__1B(A[25]), ._3__1Y(_1_s_Comp[8]), ._4__2A(A[9]), ._5__2B(A[25]),
    ._6__2Y(_1_s_Comp[9]), ._13__4B(A[25]), ._12__4A(A[11]), ._11__4Y(_1_s_Comp[11]), ._10__3B(A[25]),
    ._9__3A(A[10]), ._8__3Y(_1_s_Comp[10]));  // open: _7__GND, _14__Vcc
  _7486 u_7486_6 (
    ._1__1A(A[24]), ._2__1B(A[25]), ._3__1Y(_1_s_Comp[24]), ._5__2B(A[25]), ._13__4B(A[25]), ._10__3B(A[25]));  // open: _4__2A, _6__2Y, _7__GND, _14__Vcc, _12__4A, _11__4Y, _9__3A, _8__3Y
  assign bit_extender_1_out = {{24{1'b0}}, 1'b0};  // Bit_Extender bit_extender_1
  Adder #(.width(25)) adder_1 (.a(_1_s_Comp), .b(bit_extender_1_out), .out(ABS), .cin(A[25]));  // open: cout
  _7486 u_7486_7 (
    ._1__1A(A[12]), ._2__1B(A[25]), ._3__1Y(_1_s_Comp[12]), ._4__2A(A[13]), ._5__2B(A[25]),
    ._6__2Y(_1_s_Comp[13]), ._13__4B(A[25]), ._12__4A(A[15]), ._11__4Y(_1_s_Comp[15]), ._10__3B(A[25]),
    ._9__3A(A[14]), ._8__3Y(_1_s_Comp[14]));  // open: _7__GND, _14__Vcc
  // Probe on ABS

  // Other names for the same wires on the sheet: Y0 = _1_s_Comp[0]; Y1 = _1_s_Comp[1]; Y2 = _1_s_Comp[2];
  //   Y3 = _1_s_Comp[3]; Y4 = _1_s_Comp[4]; Y5 = _1_s_Comp[5]; Y6 = _1_s_Comp[6]; Y7 = _1_s_Comp[7];
  //   Y8 = _1_s_Comp[8]; Y9 = _1_s_Comp[9]; Y10 = _1_s_Comp[10]; Y11 = _1_s_Comp[11]; Y12 = _1_s_Comp[12];
  //   Y13 = _1_s_Comp[13]; Y14 = _1_s_Comp[14]; Y15 = _1_s_Comp[15]; Y16 = _1_s_Comp[16]; Y17 = _1_s_Comp[17];
  //   Y18 = _1_s_Comp[18]; Y19 = _1_s_Comp[19]; Y20 = _1_s_Comp[20]; Y21 = _1_s_Comp[21]; Y22 = _1_s_Comp[22];
  //   Y23 = _1_s_Comp[23]; Y24 = _1_s_Comp[24]; Sign = A[25]
endmodule

module _24_bit_MUX (
  input  [23:0] B,
  input  [23:0] A,
  input  S,
  output [23:0] Y
);

  _74157 u_74157_1 (
    ._1__S(S), ._2__A1(A[0]), ._3__B1(B[0]), ._4__Y1(Y[0]), ._5__A2(A[1]), ._6__B2(B[1]), ._7__Y2(Y[1]),
    ._15__G(1'b0), ._14__A4(A[3]), ._13__B4(B[3]), ._12__Y4(Y[3]), ._11__A3(A[2]), ._10__B3(B[2]),
    ._9__Y3(Y[2]));  // open: _8__GND, _16__Vcc
  _74157 u_74157_2 (
    ._1__S(S), ._2__A1(A[4]), ._3__B1(B[4]), ._4__Y1(Y[4]), ._5__A2(A[5]), ._6__B2(B[5]), ._7__Y2(Y[5]),
    ._15__G(1'b0), ._14__A4(A[7]), ._13__B4(B[7]), ._12__Y4(Y[7]), ._11__A3(A[6]), ._10__B3(B[6]),
    ._9__Y3(Y[6]));  // open: _8__GND, _16__Vcc
  _74157 u_74157_3 (
    ._1__S(S), ._2__A1(A[8]), ._3__B1(B[8]), ._4__Y1(Y[8]), ._5__A2(A[9]), ._6__B2(B[9]), ._7__Y2(Y[9]),
    ._15__G(1'b0), ._14__A4(A[11]), ._13__B4(B[11]), ._12__Y4(Y[11]), ._11__A3(A[10]), ._10__B3(B[10]),
    ._9__Y3(Y[10]));  // open: _8__GND, _16__Vcc
  _74157 u_74157_4 (
    ._1__S(S), ._2__A1(A[12]), ._3__B1(B[12]), ._4__Y1(Y[12]), ._5__A2(A[13]), ._6__B2(B[13]),
    ._7__Y2(Y[13]), ._15__G(1'b0), ._14__A4(A[15]), ._13__B4(B[15]), ._12__Y4(Y[15]), ._11__A3(A[14]),
    ._10__B3(B[14]), ._9__Y3(Y[14]));  // open: _8__GND, _16__Vcc
  _74157 u_74157_5 (
    ._1__S(S), ._2__A1(A[16]), ._3__B1(B[16]), ._4__Y1(Y[16]), ._5__A2(A[17]), ._6__B2(B[17]),
    ._7__Y2(Y[17]), ._15__G(1'b0), ._14__A4(A[19]), ._13__B4(B[19]), ._12__Y4(Y[19]), ._11__A3(A[18]),
    ._10__B3(B[18]), ._9__Y3(Y[18]));  // open: _8__GND, _16__Vcc
  _74157 u_74157_6 (
    ._1__S(S), ._2__A1(A[20]), ._3__B1(B[20]), ._4__Y1(Y[20]), ._5__A2(A[21]), ._6__B2(B[21]),
    ._7__Y2(Y[21]), ._15__G(1'b0), ._14__A4(A[23]), ._13__B4(B[23]), ._12__Y4(Y[23]), ._11__A3(A[22]),
    ._10__B3(B[22]), ._9__Y3(Y[22]));  // open: _8__GND, _16__Vcc
endmodule

module _11_bit_MUX (
  input  [10:0] B,
  input  [10:0] A,
  input  S,
  output [10:0] Y
);

  _74157 u_74157_1 (
    ._1__S(S), ._2__A1(A[0]), ._3__B1(B[0]), ._4__Y1(Y[0]), ._5__A2(A[1]), ._6__B2(B[1]), ._7__Y2(Y[1]),
    ._15__G(1'b0), ._14__A4(A[3]), ._13__B4(B[3]), ._12__Y4(Y[3]), ._11__A3(A[2]), ._10__B3(B[2]),
    ._9__Y3(Y[2]));  // open: _8__GND, _16__Vcc
  _74157 u_74157_2 (
    ._1__S(S), ._2__A1(A[4]), ._3__B1(B[4]), ._4__Y1(Y[4]), ._5__A2(A[5]), ._6__B2(B[5]), ._7__Y2(Y[5]),
    ._15__G(1'b0), ._14__A4(A[7]), ._13__B4(B[7]), ._12__Y4(Y[7]), ._11__A3(A[6]), ._10__B3(B[6]),
    ._9__Y3(Y[6]));  // open: _8__GND, _16__Vcc
  _74157 u_74157_3 (
    ._1__S(S), ._2__A1(A[8]), ._3__B1(B[8]), ._4__Y1(Y[8]), ._5__A2(A[9]), ._6__B2(B[9]), ._7__Y2(Y[9]),
    ._15__G(1'b0), ._11__A3(A[10]), ._10__B3(B[10]), ._9__Y3(Y[10]));  // open: _8__GND, _16__Vcc, _14__A4, _13__B4, _12__Y4
endmodule
